// Logisim project zaid.circ as structural Verilog: 5 circuits, main circuit main
module main (
  input  in_1,
  input  in_2,
  input  in_3
);

  wire clock_1_out;
  wire [31:0] adder_1_out, register_1_q, rom_1_data;

  Register #(.width(32)) register_1 (.D(adder_1_out), .en(in_1), .Q(register_1_q), .clk(clock_1_out), .clr(in_2));
  Clock clock_1 (.out(clock_1_out));
  // Probe on register_1_q
  Adder #(.width(32)) adder_1 (.a(register_1_q), .b(32'h4), .out(adder_1_out));  // open: cin, cout
  // Probe on rom_1_data
  ROM #(.addrWidth(24), .dataWidth(32)) rom_1 (.addr(register_1_q[25:2]), .data(rom_1_data), .sel(in_3));
  Control_Decoder control_decoder_1 (._32bit_instruction(rom_1_data));  // open: lb, lh, lui, lw, lbu, lhu, sb, sh, rd, sw, addi, slli, slti, sltiu, rs1, xori, srli, srai, rs2, ori, andi, add, sub, sll, slt, sltu, xor, srl, sra, or, and, beq, bne, blt, bge, bltu, bgeu, _32bit_immediate, auipc, jal, jalr
endmodule

module decoder (
  input  [31:0] _32_bit_instructions,
  output [6:0] opcode,
  output [4:0] rd,
  output [2:0] func_3,
  output [4:0] rs1,
  output [4:0] rs2,
  output [6:0] func_7
);


  assign func_3 = _32_bit_instructions[14:12];
  assign func_7 = _32_bit_instructions[31:25];
  assign opcode = _32_bit_instructions[6:0];
  assign rd = _32_bit_instructions[11:7];
  assign rs1 = _32_bit_instructions[19:15];
  assign rs2 = _32_bit_instructions[24:20];
endmodule

module Control_Unit (
  input  [6:0] in_1,
  input  [2:0] in_2,
  input  [1:0] in_3,
  output lb,
  output lh,
  output lw,
  output sb,
  output lbu,
  output sh,
  output lhu,
  output sw,
  output addi,
  output slli,
  output slti,
  output sltiu,
  output xori,
  output srli,
  output srai,
  output ori,
  output andi,
  output add,
  output sub,
  output sll,
  output slt,
  output sltu,
  output \xor ,
  output \or ,
  output \and ,
  output srl,
  output sra,
  output jalr,
  output auipc,
  output beq,
  output bne,
  output blt,
  output bge,
  output bltu,
  output lui,
  output bgeu,
  output jal
);

  wire comparator_1_eq, comparator_2_eq, comparator_3_eq, comparator_4_eq, comparator_7_eq,
       demultiplexer_1_out0, demultiplexer_1_out5, demultiplexer_4_out5;

  Comparator #(.width(7)) comparator_1 (.a(7'b0110011), .b(in_1), .eq(comparator_1_eq));  // open: gt, lt
  Demultiplexer #(.select(4), .enable("false")) demultiplexer_1 (
    .out0(demultiplexer_1_out0), .out1(sll), .out2(slt), .out3(sltu), .out4(\xor ),
    .out5(demultiplexer_1_out5), .out6(demultiplexer_1_out5), .out7(\or ), .out8(\and ),
    .in(comparator_1_eq), .sel({1'b0, in_2}));  // open: out9, out10, out11, out12, out13, out14, out15
  Comparator #(.width(7)) comparator_2 (.a(7'b1100011), .b(in_1), .eq(comparator_2_eq));  // open: gt, lt
  Demultiplexer #(.select(3), .enable("false")) demultiplexer_2 (
    .out0(beq), .out1(bne), .out4(blt), .out5(bge), .out6(bltu), .out7(bgeu), .in(comparator_2_eq), .sel(in_2));  // open: out2, out3
  Comparator #(.width(7)) comparator_3 (.a(7'b0000011), .b(in_1), .eq(comparator_3_eq));  // open: gt, lt
  Comparator #(.width(7)) comparator_4 (.a(7'b0010011), .b(in_1), .eq(comparator_4_eq));  // open: gt, lt
  Demultiplexer #(.select(3), .enable("false")) demultiplexer_3 (
    .out0(lb), .out1(lh), .out2(lw), .out3(lbu), .out4(lhu), .in(comparator_3_eq), .sel(in_2));  // open: out5, out6, out7
  Demultiplexer #(.select(4), .enable("false")) demultiplexer_4 (
    .out0(addi), .out1(slli), .out2(slti), .out3(sltiu), .out4(xori), .out5(demultiplexer_4_out5),
    .out6(demultiplexer_4_out5), .out7(ori), .out8(andi), .in(comparator_4_eq), .sel({1'b0, in_2}));  // open: out9, out10, out11, out12, out13, out14, out15
  Demultiplexer #(.select(2), .enable("false")) demultiplexer_5 (
    .out0(srl), .out1(sra), .in(demultiplexer_1_out5), .sel(in_3));  // open: out2, out3
  Demultiplexer #(.select(2), .enable("false")) demultiplexer_6 (
    .out0(add), .out1(sub), .in(demultiplexer_1_out0), .sel(in_3));  // open: out2, out3
  Demultiplexer #(.select(2), .enable("false")) demultiplexer_7 (
    .out0(srli), .out1(srai), .in(demultiplexer_4_out5), .sel(in_3));  // open: out2, out3
  Comparator #(.width(7)) comparator_5 (.a(7'b1100111), .b(in_1), .eq(jalr));  // open: gt, lt
  Comparator #(.width(7)) comparator_6 (.a(7'b1101111), .b(in_1), .eq(jal));  // open: gt, lt
  Comparator #(.width(7)) comparator_7 (.a(7'b0100011), .b(in_1), .eq(comparator_7_eq));  // open: gt, lt
  Demultiplexer #(.select(2), .enable("false")) demultiplexer_8 (
    .out0(sb), .out1(sh), .out2(sw), .in(comparator_7_eq), .sel(in_2[1:0]));  // open: out3
  Comparator #(.width(7)) comparator_8 (.a(7'b0010111), .b(in_1), .eq(auipc));  // open: gt, lt
  Comparator #(.width(7)) comparator_9 (.a(7'b0110111), .b(in_1), .eq(lui));  // open: gt, lt

  // Other names for the same wires on the sheet: _14_12_FUNC_3[2:0] = in_2; _30_31_FUNC_7[1:0] = in_3;
  //   Opcode[6:0] = in_1

  // Notes on the sheet:
  //   r-type
  //   sb-type
  //   load i-type
  //   alu i-type
  //   JALR i-type
  //   JAL uj-type
  //   s-type
  //   AUIPC u-type
  //   LUI u-type
endmodule

// sw
module Control_Decoder (
  input  [31:0] _32bit_instruction,
  output lb,
  output lh,
  output lw,
  output lbu,
  output lhu,
  output sb,
  output sh,
  output [4:0] rd,
  output sw,
  output addi,
  output slli,
  output slti,
  output sltiu,
  output [4:0] rs1,
  output xori,
  output srli,
  output srai,
  output [4:0] rs2,
  output ori,
  output andi,
  output add,
  output sub,
  output sll,
  output slt,
  output sltu,
  output \xor ,
  output srl,
  output sra,
  output \or ,
  output \and ,
  output beq,
  output bne,
  output lui,
  output blt,
  output bge,
  output bltu,
  output bgeu,
  output auipc,
  output jal,
  output jalr,
  output [31:0] _32bit_immediate
);

  wire [2:0] decoder_1_func_3;
  wire [6:0] decoder_1_func_7, decoder_1_opcode;

  decoder decoder_1 (
    ._32_bit_instructions(_32bit_instruction), .opcode(decoder_1_opcode), .rd(rd), .func_3(decoder_1_func_3),
    .rs1(rs1), .rs2(rs2), .func_7(decoder_1_func_7));
  // Probe on decoder_1_opcode
  immediate_generation immediate_generation_1 (
    .in_1(decoder_1_opcode), .in_2(_32bit_instruction), .out_3(_32bit_immediate));
  Control_Unit control_unit_1 (
    .in_1(decoder_1_opcode), .in_2(decoder_1_func_3), .in_3(decoder_1_func_7[6:5]), .lb(lb), .lh(lh),
    .lw(lw), .lbu(lbu), .lhu(lhu), .addi(addi), .slli(slli), .slti(slti), .sltiu(sltiu), .xori(xori),
    .srli(srli), .srai(srai), .sb(sb), .sh(sh), .sw(sw), .add(add), .sub(sub), .sll(sll), .slt(slt),
    .sltu(sltu), .\xor (\xor ), .srl(srl), .sra(sra), .\or (\or ), .\and (\and ), .beq(beq), .bne(bne),
    .blt(blt), .bge(bge), .bltu(bltu), .bgeu(bgeu), .jalr(jalr), .jal(jal), .auipc(auipc), .lui(lui),
    .ori(ori), .andi(andi));
endmodule

module immediate_generation (
  input  [6:0] in_1,
  input  [31:0] in_2,
  output [31:0] out_3
);

  wire comparator_1_eq, comparator_2_eq, comparator_3_eq, comparator_4_eq, comparator_5_eq, comparator_6_eq,
       comparator_7_eq, or_1_out;
  wire [2:0] controlled_buffer_6_out;
  wire [11:0] controlled_buffer_1_out, controlled_buffer_3_out;
  wire [12:0] controlled_buffer_4_out;
  wire [20:0] controlled_buffer_2_out;
  wire [31:0] bit_extender_1_out, bit_extender_2_out, bit_extender_3_out, bit_extender_4_out,
       controlled_buffer_5_out;

  Comparator #(.width(7)) comparator_1 (.a(7'b0000011), .b(in_1), .eq(comparator_1_eq));  // open: gt, lt
  Comparator #(.width(7)) comparator_2 (.a(7'b0010011), .b(in_1), .eq(comparator_2_eq));  // open: gt, lt
  Comparator #(.width(7)) comparator_3 (.a({7{1'b1}}), .b(in_1), .eq(comparator_3_eq));  // open: gt, lt
  Comparator #(.width(7)) comparator_4 (.a(7'b0100011), .b(in_1), .eq(comparator_4_eq));  // open: gt, lt
  Comparator #(.width(7)) comparator_5 (.a(7'b1100011), .b(in_1), .eq(comparator_5_eq));  // open: gt, lt
  Comparator #(.width(7)) comparator_6 (.a(7'b1101111), .b(in_1), .eq(comparator_6_eq));  // open: gt, lt
  Comparator #(.width(7)) comparator_7 (.a(7'b0110111), .b(in_1), .eq(comparator_7_eq));  // open: gt, lt
  or or_1 (or_1_out, comparator_1_eq, comparator_2_eq, comparator_3_eq);
  // Probe on {in_2[31:25], in_2[11:7]}
  assign controlled_buffer_1_out = or_1_out ? in_2[31:20] : 12'bz;  // Controlled_Buffer controlled_buffer_1
  assign controlled_buffer_2_out = comparator_7_eq ? {in_2[31], in_2[19:12], in_2[20], in_2[30:21], 1'b0} : 21'bz;  // Controlled_Buffer controlled_buffer_2
  // Probe on controlled_buffer_1_out
  assign controlled_buffer_3_out = comparator_4_eq ? {in_2[31:25], in_2[11:7]} : 12'bz;  // Controlled_Buffer controlled_buffer_3
  // Probe on controlled_buffer_4_out
  assign controlled_buffer_4_out = comparator_5_eq ? {in_2[31], in_2[7], in_2[30:25], in_2[11:8], 1'b0} : 13'bz;  // Controlled_Buffer controlled_buffer_4
  // Probe on {in_2[31:12], {12{1'b0}}}
  assign controlled_buffer_5_out = comparator_6_eq ? {in_2[31:12], {12{1'b0}}} : 32'bz;  // Controlled_Buffer controlled_buffer_5
  assign controlled_buffer_6_out = or_1_out ? 3'b000 : 3'bz;  // Controlled_Buffer controlled_buffer_6
  assign bit_extender_1_out = {{20{controlled_buffer_1_out[11]}}, controlled_buffer_1_out};  // Bit_Extender bit_extender_1
  // Probe on bit_extender_2_out
  assign bit_extender_2_out = {{20{controlled_buffer_3_out[11]}}, controlled_buffer_3_out};  // Bit_Extender bit_extender_2
  assign controlled_buffer_6_out = comparator_4_eq ? 3'b001 : 3'bz;  // Controlled_Buffer controlled_buffer_7
  assign bit_extender_3_out = {{19{controlled_buffer_4_out[12]}}, controlled_buffer_4_out};  // Bit_Extender bit_extender_3
  assign controlled_buffer_6_out = comparator_5_eq ? 3'b010 : 3'bz;  // Controlled_Buffer controlled_buffer_8
  assign controlled_buffer_6_out = comparator_6_eq ? 3'b011 : 3'bz;  // Controlled_Buffer controlled_buffer_9
  assign bit_extender_4_out = {{11{controlled_buffer_2_out[20]}}, controlled_buffer_2_out};  // Bit_Extender bit_extender_4
  assign controlled_buffer_6_out = comparator_7_eq ? 3'b100 : 3'bz;  // Controlled_Buffer controlled_buffer_10
  Multiplexer #(.select(3), .width(32), .enable("false")) multiplexer_1 (
    .in0(bit_extender_1_out), .in1(bit_extender_2_out), .in2(bit_extender_3_out),
    .in3(controlled_buffer_5_out), .in4(bit_extender_4_out), .out(out_3), .sel(controlled_buffer_6_out));  // open: in5, in6, in7

  // Notes on the sheet:
  //   load i-type
  //   alu i-type
  //   jalr i-type
  //   store
  //   SB-type
  //   jal UJ-type
  //   auipc/lui U-type
endmodule
